# Fritzing sketch esquema proyecto llenado botellas (saved by Fritzing 0.9.3b)

parts:
  Componente1 = Arduino Mega ADK (Rev3)
  M1 = Stepper Motor - Unipolar
  DRV_1 = DRV 8825 Stepper Motor Carrier, High Current [part_number="DRV 8825"]
  C1 = Electrolytic Capacitor [capacitance=1000μF package="1010 [SMD, electrolytic]"]
  Power_plug1 = Power plug
  J1 = Infrared Proximity Sensor
  WeMos_D1_Mini_Relay_Shield_V1 = WeMos D1 Mini Relay Shield V2  # not connected

nets:
  5V: Componente1.5V, J1.Vcc
  N1: Componente1.D3_PWM, J1.Vout
  N2: M1.A, DRV_1.OUT_2B
  N3: M1.C, DRV_1.OUT_2A
  N4: M1.B, DRV_1.OUT_1A
  N5: M1.D, DRV_1.OUT_1B
  N6: DRV_1.VOLTAGE_ST/_MT, C1.+, Power_plug1.VCC
  N7: DRV_1.GROUND_ST/_MT, C1.-, Power_plug1.GND

notes:
  elec industrial llenado
